// Logisim project pcb_computer.circ as structural Verilog: 16 circuits, main circuit main
module main (
);

  wire Clk, Count, NotClearMicrocode, NotEnableA16, NotEnableAHigh, NotEnableALow, NotEnableALU, NotEnableB,
       NotEnableC, NotEnableIRHigh, NotEnableIRLow, NotEnablePC16, NotEnableRam, NotLoadAHigh, NotLoadALow,
       NotLoadB, NotLoadC, NotLoadIRHigh, NotLoadIRLow, NotLoadPC, NotLoadRam, por_1_out, PowerOnReset;
  wire [1:0] microcode_1_a;
  wire [7:0] B_dataout, Bus8, C_dataout, IRHigh_dataout, programcounter_1_addressout,
       programcounter_1_addressout_2;
  wire [14:2] alu_1_notcout;
  wire [15:0] addressselector_1_ramaddress, ALow_dataout;

  Clock clock_1 (.out(Clk));
  // Probe on IRHigh_dataout[7:2]
  Microcode microcode_1 (
    .NotSyncClear(NotClearMicrocode), .NotAsyncClear(PowerOnReset), .Clock(Clk), .A(microcode_1_a[0]),
    .B(microcode_1_a[1]));
  Register8 IRHigh (
    .Clock(Clk), .NotLoad(NotLoadIRHigh), .NotEnable(NotEnableIRHigh), .BusIn(Bus8), .BusOut(Bus8),
    .DataOut(IRHigh_dataout));
  Register8 IRLow (
    .Clock(Clk), .NotLoad(NotLoadIRLow), .NotEnable(NotEnableIRLow), .BusIn(Bus8), .BusOut(Bus8),
    .DataOut(alu_1_notcout[14:7]));
  Register8 AHigh (
    .Clock(Clk), .NotLoad(NotLoadAHigh), .NotEnable(NotEnableAHigh), .BusIn(Bus8), .BusOut(Bus8),
    .DataOut(ALow_dataout[15:8]));
  Register8 ALow (
    .Clock(Clk), .NotLoad(NotLoadALow), .NotEnable(NotEnableALow), .BusIn(Bus8), .BusOut(Bus8),
    .DataOut(ALow_dataout[7:0]));
  Register8 B (
    .Clock(Clk), .NotLoad(NotLoadB), .NotEnable(NotEnableB), .BusIn(Bus8), .BusOut(Bus8), .DataOut(B_dataout));
  Register8 C (
    .Clock(Clk), .NotLoad(NotLoadC), .NotEnable(NotEnableC), .BusIn(Bus8), .BusOut(Bus8), .DataOut(C_dataout));
  ALU alu_1 (
    .NotEnable(NotEnableALU), .A(B_dataout), .B(C_dataout), .Operation(IRHigh_dataout[7:2]),
    .NotCout(alu_1_notcout[2]), .Negative(alu_1_notcout[3]), .NotZero(alu_1_notcout[4]), .DataOut(Bus8));
  // Probe on ALow_dataout
  // Probe on alu_1_notcout[14:7]
  POR #(.PorHighDuration(1)) por_1 (.out(por_1_out));
  not not_1 (PowerOnReset, por_1_out);
  // Probe on {alu_1_notcout[14:7], 2'b00, alu_1_notcout[4:2], microcode_1_a}
  ROM #(.addrWidth(15), .dataWidth(20)) rom_1 (
    .addr({alu_1_notcout[14:7], 2'b00, alu_1_notcout[4:2], microcode_1_a}),
    .data({NotEnableALU, NotEnableRam, NotLoadRam, NotClearMicrocode, Count, NotLoadPC, NotEnableA16, NotEnablePC16, NotEnableC, NotLoadC, NotEnableB, NotLoadB, NotEnableALow, NotEnableAHigh, NotLoadALow, NotLoadAHigh, NotEnableIRLow, NotEnableIRHigh, NotLoadIRLow, NotLoadIRHigh}));
  ProgramCounter programcounter_1 (
    .Clock(Clk), .NotClear(PowerOnReset), .NotLoad(NotLoadPC), .Count(Count), .AddressIn(ALow_dataout),
    .AddressOut({programcounter_1_addressout_2, programcounter_1_addressout}));
  AddressSelector addressselector_1 (
    .NotEnablePC(NotEnablePC16), .PCHigh(programcounter_1_addressout_2), .PCLow(programcounter_1_addressout),
    .NotEnableA(NotEnableA16), .AHigh(ALow_dataout[15:8]), .ALow(ALow_dataout[7:0]),
    .RAMAddress(addressselector_1_ramaddress));
  // Probe on {programcounter_1_addressout_2, programcounter_1_addressout}
  // Probe on addressselector_1_ramaddress
  // Probe on Bus8
  Memory memory_1 (
    .AddressL(addressselector_1_ramaddress), .NotLoad(NotLoadRam), .NotEnable(NotEnableRam), .Clock(Clk),
    .DataIn(Bus8), .DataOut(Bus8));
  // Probe on Bus8

  // Notes on the sheet:
  //   contents of rom_1 (hex, n*v repeats v):
  //   beffd b6ffe edfff fefff beffd b6ffe edfff fefff beffd b6ffe edfff fefff beffd b6ffe edfff fefff
  //   beffd b6ffe edfff fefff beffd b6ffe edfff fefff beffd b6ffe edfff fefff beffd b6ffe edfff fefff
  //   beffd b6ffe edfff fefff beffd b6ffe edfff fefff beffd b6ffe edfff fefff beffd b6ffe edfff fefff
  //   beffd b6ffe edfff fefff beffd b6ffe edfff fefff beffd b6ffe edfff fefff beffd b6ffe edfff fefff
  //   beffd b6ffe edfff fefff beffd b6ffe edfff fefff beffd b6ffe edfff fefff beffd b6ffe edfff fefff
  //   beffd b6ffe edfff fefff beffd b6ffe edfff fefff beffd b6ffe edfff fefff beffd b6ffe edfff fefff
  //   beffd b6ffe edfff fefff beffd b6ffe edfff fefff beffd b6ffe edfff fefff beffd b6ffe edfff fefff
  //   beffd b6ffe edfff fefff beffd b6ffe edfff fefff beffd b6ffe edfff fefff beffd b6ffe edfff fefff
  //   beffd b6ffe edfff fefff beffd b6ffe edfff fefff beffd b6ffe edfff fefff beffd b6ffe edfff fefff
  //   beffd b6ffe edfff fefff beffd b6ffe edfff fefff beffd b6ffe edfff fefff beffd b6ffe edfff fefff
  //   beffd b6ffe edfff fefff beffd b6ffe edfff fefff beffd b6ffe edfff fefff beffd b6ffe edfff fefff
  //   beffd b6ffe edfff fefff beffd b6ffe edfff fefff beffd b6ffe edfff fefff beffd b6ffe edfff fefff
  //   beffd b6ffe edfff fefff beffd b6ffe edfff fefff beffd b6ffe edfff fefff beffd b6ffe edfff fefff
  //   beffd b6ffe edfff fefff beffd b6ffe edfff fefff beffd b6ffe edfff fefff beffd b6ffe edfff fefff
  //   beffd b6ffe edfff fefff beffd b6ffe edfff fefff beffd b6ffe edfff fefff beffd b6ffe edfff fefff
  //   beffd b6ffe edfff fefff beffd b6ffe edfff fefff beffd b6ffe edfff fefff beffd b6ffe edfff fefff
  //   beffd b6ffe edfbf fefbf beffd b6ffe edfbf fefbf beffd b6ffe edfbf fefbf beffd b6ffe edfbf fefbf
  //   beffd b6ffe edfbf fefbf beffd b6ffe edfbf fefbf beffd b6ffe edfbf fefbf beffd b6ffe edfbf fefbf
  //   beffd b6ffe edfbf fefbf beffd b6ffe edfbf fefbf beffd b6ffe edfbf fefbf beffd b6ffe edfbf fefbf
  //   beffd b6ffe edfbf fefbf beffd b6ffe edfbf fefbf beffd b6ffe edfbf fefbf beffd b6ffe edfbf fefbf
  //   beffd b6ffe edfbf fefbf beffd b6ffe edfbf fefbf beffd b6ffe edfbf fefbf beffd b6ffe edfbf fefbf
  //   beffd b6ffe edfbf fefbf beffd b6ffe edfbf fefbf beffd b6ffe edfbf fefbf beffd b6ffe edfbf fefbf
  //   beffd b6ffe edfbf fefbf beffd b6ffe edfbf fefbf beffd b6ffe edfbf fefbf beffd b6ffe edfbf fefbf
  //   beffd b6ffe edfbf fefbf beffd b6ffe edfbf fefbf beffd b6ffe edfbf fefbf beffd b6ffe edfbf fefbf
  //   beffd b6ffe edfbf fefbf beffd b6ffe edfbf fefbf beffd b6ffe edfbf fefbf beffd b6ffe edfbf fefbf
  //   beffd b6ffe edfbf fefbf beffd b6ffe edfbf fefbf beffd b6ffe edfbf fefbf beffd b6ffe edfbf fefbf
  //   beffd b6ffe edfbf fefbf beffd b6ffe edfbf fefbf beffd b6ffe edfbf fefbf beffd b6ffe edfbf fefbf
  //   beffd b6ffe edfbf fefbf beffd b6ffe edfbf fefbf beffd b6ffe edfbf fefbf beffd b6ffe edfbf fefbf
  //   beffd b6ffe edfbf fefbf beffd b6ffe edfbf fefbf beffd b6ffe edfbf fefbf beffd b6ffe edfbf fefbf
  //   beffd b6ffe edfbf fefbf beffd b6ffe edfbf fefbf beffd b6ffe edfbf fefbf beffd b6ffe edfbf fefbf
  //   beffd b6ffe edfbf fefbf beffd b6ffe edfbf fefbf beffd b6ffe edfbf fefbf beffd b6ffe edfbf fefbf
  //   beffd b6ffe edfbf fefbf beffd b6ffe edfbf fefbf beffd b6ffe edfbf fefbf beffd b6ffe edfbf fefbf
  //   beffd b6ffe edf7f fef7f beffd b6ffe edf7f fef7f beffd b6ffe edf7f fef7f beffd b6ffe edf7f fef7f
  //   beffd b6ffe edf7f fef7f beffd b6ffe edf7f fef7f beffd b6ffe edf7f fef7f beffd b6ffe edf7f fef7f
  //   beffd b6ffe edf7f fef7f beffd b6ffe edf7f fef7f beffd b6ffe edf7f fef7f beffd b6ffe edf7f fef7f
  //   beffd b6ffe edf7f fef7f beffd b6ffe edf7f fef7f beffd b6ffe edf7f fef7f beffd b6ffe edf7f fef7f
  //   beffd b6ffe edf7f fef7f beffd b6ffe edf7f fef7f beffd b6ffe edf7f fef7f beffd b6ffe edf7f fef7f
  //   beffd b6ffe edf7f fef7f beffd b6ffe edf7f fef7f beffd b6ffe edf7f fef7f beffd b6ffe edf7f fef7f
  //   beffd b6ffe edf7f fef7f beffd b6ffe edf7f fef7f beffd b6ffe edf7f fef7f beffd b6ffe edf7f fef7f
  //   beffd b6ffe edf7f fef7f beffd b6ffe edf7f fef7f beffd b6ffe edf7f fef7f beffd b6ffe edf7f fef7f
  //   beffd b6ffe edf7f fef7f beffd b6ffe edf7f fef7f beffd b6ffe edf7f fef7f beffd b6ffe edf7f fef7f
  //   beffd b6ffe edf7f fef7f beffd b6ffe edf7f fef7f beffd b6ffe edf7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
endmodule

module OctalTransceiver74245 (
  input  [7:0] B_in,
  input  NotEnable,
  input  Dir,
  input  [7:0] A_in,
  output [7:0] B_Out,
  output [7:0] A_out
);

  wire and_1_out, and_2_out, not_1_out, not_2_out, not_3_out;

  not not_1 (not_1_out, Dir);
  not not_2 (not_2_out, NotEnable);
  and and_1 (and_1_out, not_1_out, not_2_out);
  and and_2 (and_2_out, Dir, not_3_out);
  not not_3 (not_3_out, NotEnable);
  assign A_out[0] = and_1_out ? B_in[0] : 1'bz;  // Controlled_Buffer controlled_buffer_1
  assign A_out[1] = and_1_out ? B_in[1] : 1'bz;  // Controlled_Buffer controlled_buffer_2
  assign B_Out[0] = and_2_out ? A_in[0] : 1'bz;  // Controlled_Buffer controlled_buffer_3
  assign B_Out[1] = and_2_out ? A_in[1] : 1'bz;  // Controlled_Buffer controlled_buffer_4
  assign A_out[2] = and_1_out ? B_in[2] : 1'bz;  // Controlled_Buffer controlled_buffer_5
  assign A_out[3] = and_1_out ? B_in[3] : 1'bz;  // Controlled_Buffer controlled_buffer_6
  assign B_Out[2] = and_2_out ? A_in[2] : 1'bz;  // Controlled_Buffer controlled_buffer_7
  assign B_Out[3] = and_2_out ? A_in[3] : 1'bz;  // Controlled_Buffer controlled_buffer_8
  assign A_out[4] = and_1_out ? B_in[4] : 1'bz;  // Controlled_Buffer controlled_buffer_9
  assign A_out[5] = and_1_out ? B_in[5] : 1'bz;  // Controlled_Buffer controlled_buffer_10
  assign B_Out[4] = and_2_out ? A_in[4] : 1'bz;  // Controlled_Buffer controlled_buffer_11
  assign B_Out[5] = and_2_out ? A_in[5] : 1'bz;  // Controlled_Buffer controlled_buffer_12
  assign A_out[6] = and_1_out ? B_in[6] : 1'bz;  // Controlled_Buffer controlled_buffer_13
  assign A_out[7] = and_1_out ? B_in[7] : 1'bz;  // Controlled_Buffer controlled_buffer_14
  assign B_Out[6] = and_2_out ? A_in[6] : 1'bz;  // Controlled_Buffer controlled_buffer_15
  assign B_Out[7] = and_2_out ? A_in[7] : 1'bz;  // Controlled_Buffer controlled_buffer_16
endmodule

module Register8 (
  input  Clock,
  input  NotLoad,
  input  NotEnable,
  input  [7:0] BusIn,
  output [7:0] BusOut,
  output [7:0] DataOut
);

  OctalTransceiver74245 octaltransceiver74245_1 (
    .B_Out(BusOut), .A_out(DataOut), .Dir(1'b1), .NotEnable(NotEnable), .B_in(BusOut), .A_in(DataOut));
  _74377 #(.ShowInternalStructure("true")) u_74377_1 (
    .pin1(NotLoad), .pin2(DataOut[0]), .pin3(BusIn[0]), .pin4(BusIn[1]), .pin5(DataOut[1]),
    .pin6(DataOut[2]), .pin7(BusIn[2]), .pin8(BusIn[3]), .pin9(DataOut[3]), .pin19(DataOut[7]),
    .pin18(BusIn[7]), .pin17(BusIn[6]), .pin16(DataOut[6]), .pin15(DataOut[5]), .pin14(BusIn[5]),
    .pin13(BusIn[4]), .pin12(DataOut[4]), .pin11(Clock));
  // Probe on DataOut
endmodule

module ProgramCounter (
  input  Clock,
  input  NotClear,
  input  NotLoad,
  input  Count,
  input  [15:0] AddressIn,
  output [15:0] AddressOut
);

  wire n74161_1_pin15, n74161_2_pin15, n74161_3_pin15;

  _74161 #(.ShowInternalStructure("true")) u_74161_1 (
    .pin1(NotClear), .pin2(Clock), .pin3(AddressIn[0]), .pin4(AddressIn[1]), .pin5(AddressIn[2]),
    .pin6(AddressIn[3]), .pin7(Count), .pin15(n74161_1_pin15), .pin14(AddressOut[0]), .pin13(AddressOut[1]),
    .pin12(AddressOut[2]), .pin11(AddressOut[3]), .pin10(NotLoad), .pin9(NotLoad));
  _74161 #(.ShowInternalStructure("true")) u_74161_2 (
    .pin1(NotClear), .pin2(Clock), .pin3(AddressIn[4]), .pin4(AddressIn[5]), .pin5(AddressIn[6]),
    .pin6(AddressIn[7]), .pin7(Count), .pin15(n74161_2_pin15), .pin14(AddressOut[4]), .pin13(AddressOut[5]),
    .pin12(AddressOut[6]), .pin11(AddressOut[7]), .pin10(n74161_1_pin15), .pin9(NotLoad));
  _74161 #(.ShowInternalStructure("true")) u_74161_3 (
    .pin1(NotClear), .pin2(Clock), .pin3(AddressIn[8]), .pin4(AddressIn[9]), .pin5(AddressIn[10]),
    .pin6(AddressIn[11]), .pin7(Count), .pin15(n74161_3_pin15), .pin14(AddressOut[8]), .pin13(AddressOut[9]),
    .pin12(AddressOut[10]), .pin11(AddressOut[11]), .pin10(n74161_2_pin15), .pin9(NotLoad));
  _74161 #(.ShowInternalStructure("true")) u_74161_4 (
    .pin1(NotClear), .pin2(Clock), .pin3(AddressIn[12]), .pin4(AddressIn[13]), .pin5(AddressIn[14]),
    .pin6(AddressIn[15]), .pin7(Count), .pin14(AddressOut[12]), .pin13(AddressOut[13]),
    .pin12(AddressOut[14]), .pin11(AddressOut[15]), .pin10(n74161_3_pin15), .pin9(NotLoad));  // open: pin15

  // Other names for the same wires on the sheet: Clk = Clock; nClr = NotClear; nLD = NotLoad
endmodule

module Bus16 (
  input  NotEnablePC,
  input  [7:0] PCHigh,
  input  [7:0] PCLow,
  input  NotEnableA,
  input  [7:0] AHigh,
  input  [7:0] ALow,
  output [15:0] RAMAddress
);

  OctalTransceiver74245 octaltransceiver74245_1 (
    .B_Out(PCHigh), .A_out(RAMAddress[15:8]), .Dir(1'b0), .NotEnable(NotEnablePC), .B_in(PCHigh),
    .A_in(RAMAddress[15:8]));
  OctalTransceiver74245 octaltransceiver74245_2 (
    .B_Out(PCLow), .A_out(RAMAddress[7:0]), .Dir(1'b0), .NotEnable(NotEnablePC), .B_in(PCLow),
    .A_in(RAMAddress[7:0]));
  OctalTransceiver74245 octaltransceiver74245_3 (
    .B_Out(AHigh), .A_out(RAMAddress[15:8]), .Dir(1'b0), .NotEnable(NotEnableA), .B_in(AHigh),
    .A_in(RAMAddress[15:8]));
  OctalTransceiver74245 octaltransceiver74245_4 (
    .B_Out(ALow), .A_out(RAMAddress[7:0]), .Dir(1'b0), .NotEnable(NotEnableA), .B_in(ALow),
    .A_in(RAMAddress[7:0]));
endmodule

module AddressSelector (
  input  NotEnablePC,
  input  [7:0] PCHigh,
  input  [7:0] PCLow,
  input  NotEnableA,
  input  [7:0] AHigh,
  input  [7:0] ALow,
  output [15:0] RAMAddress
);

  OctalTransceiver74245 octaltransceiver74245_1 (
    .B_Out(PCHigh), .A_out(RAMAddress[15:8]), .Dir(1'b0), .NotEnable(NotEnablePC), .B_in(PCHigh),
    .A_in(RAMAddress[15:8]));
  OctalTransceiver74245 octaltransceiver74245_2 (
    .B_Out(PCLow), .A_out(RAMAddress[7:0]), .Dir(1'b0), .NotEnable(NotEnablePC), .B_in(PCLow),
    .A_in(RAMAddress[7:0]));
  OctalTransceiver74245 octaltransceiver74245_3 (
    .B_Out(AHigh), .A_out(RAMAddress[15:8]), .Dir(1'b0), .NotEnable(NotEnableA), .B_in(AHigh),
    .A_in(RAMAddress[15:8]));
  OctalTransceiver74245 octaltransceiver74245_4 (
    .B_Out(ALow), .A_out(RAMAddress[7:0]), .Dir(1'b0), .NotEnable(NotEnableA), .B_in(ALow),
    .A_in(RAMAddress[7:0]));
endmodule

module Microcode (
  input  NotSyncClear,
  input  NotAsyncClear,
  input  Clock,
  output A,
  output B
);

  wire n74161_1_pin3, n74161_1_pin7;

  _74161 u_74161_1 (
    .pin1(NotAsyncClear), .pin2(Clock), .pin3(n74161_1_pin3), .pin4(n74161_1_pin3), .pin5(n74161_1_pin3),
    .pin6(n74161_1_pin3), .pin7(n74161_1_pin7), .pin14(A), .pin13(B), .pin10(n74161_1_pin7),
    .pin9(NotSyncClear));  // open: pin15, pin12, pin11
  // also tied to GND on the sheet: n74161_1_pin3
  // also tied to VCC on the sheet: n74161_1_pin7
endmodule

module RAM_2 (
  input  Clock,
  input  [7:0] DataInL,
  input  WriteL,
  input  AddressL,
  input  AddressR,
  output [7:0] DataOutR,
  output [7:0] DataOutL
);

  wire decoder_1_out0, decoder_1_out1, not_1_out;
  wire [7:0] multiplexer_1_out, register_1_q, register_2_q;

  Decoder decoder_1 (.out0(decoder_1_out0), .out1(decoder_1_out1), .sel(AddressL), .en(WriteL));
  Register register_1 (.D(DataInL), .en(decoder_1_out0), .clk(Clock), .Q(register_1_q), .clr(1'b0));
  Register register_2 (.D(DataInL), .en(decoder_1_out1), .clk(Clock), .Q(register_2_q), .clr(1'b0));
  Multiplexer #(.width(8)) multiplexer_1 (
    .in0(register_1_q), .in1(register_2_q), .out(multiplexer_1_out), .sel(AddressL));
  Multiplexer #(.width(8)) multiplexer_2 (.in0(register_1_q), .in1(register_2_q), .out(DataOutR), .sel(AddressR));
  assign DataOutL = not_1_out ? multiplexer_1_out : 8'bz;  // Controlled_Buffer controlled_buffer_1
  not not_1 (not_1_out, WriteL);
endmodule

module RAM_4 (
  input  Clock,
  input  [7:0] DataInL,
  input  NotWriteL,
  input  [1:0] AddressL,
  input  [1:0] AddressR,
  output [7:0] DataOutL,
  output [7:0] DataOutR
);

  wire decoder_1_out0, decoder_1_out1, not_1_out;
  wire [7:0] multiplexer_1_out, ram_2_1_dataoutl, ram_2_1_dataoutr, ram_2_2_dataoutl, ram_2_2_dataoutr;

  not not_1 (not_1_out, NotWriteL);
  Decoder decoder_1 (.out0(decoder_1_out0), .out1(decoder_1_out1), .sel(AddressL[1]), .en(not_1_out));
  RAM_2 ram_2_1 (
    .Clock(Clock), .DataInL(DataInL), .WriteL(decoder_1_out0), .AddressL(AddressL[0]),
    .AddressR(AddressR[0]), .DataOutR(ram_2_1_dataoutr), .DataOutL(ram_2_1_dataoutl));
  RAM_2 ram_2_2 (
    .Clock(Clock), .DataInL(DataInL), .WriteL(decoder_1_out1), .AddressL(AddressL[0]),
    .AddressR(AddressR[0]), .DataOutR(ram_2_2_dataoutr), .DataOutL(ram_2_2_dataoutl));
  Multiplexer #(.width(8)) multiplexer_1 (
    .in0(ram_2_1_dataoutl), .in1(ram_2_2_dataoutl), .out(multiplexer_1_out), .sel(AddressL[1]));
  Multiplexer #(.width(8)) multiplexer_2 (
    .in0(ram_2_1_dataoutr), .in1(ram_2_2_dataoutr), .out(DataOutR), .sel(AddressR[1]));
  assign DataOutL = NotWriteL ? multiplexer_1_out : 8'bz;  // Controlled_Buffer controlled_buffer_1
endmodule

module RAM_IDT7134 (
  input  Clock,
  input  [7:0] DataInL,
  input  NotWriteRamL,
  input  [15:0] AddressL,
  input  [15:0] AddressR,
  input  CEL,
  input  NotOutputEnableL,
  input  NotOutputEnableR,
  output [7:0] DataOutL,
  output [7:0] DataOutR
);

  wire nor_1_out, not_1_out, or_1_out;
  wire [7:0] ram_4_1_dataoutl, ram_4_1_dataoutr;

  or or_1 (or_1_out, NotWriteRamL, CEL);
  RAM_4 ram_4_1 (
    .Clock(Clock), .DataInL(DataInL), .NotWriteL(or_1_out), .AddressL(AddressL[1:0]),
    .AddressR(AddressR[1:0]), .DataOutL(ram_4_1_dataoutl), .DataOutR(ram_4_1_dataoutr));
  assign DataOutL = nor_1_out ? ram_4_1_dataoutl : 8'bz;  // Controlled_Buffer controlled_buffer_1
  nor nor_1 (nor_1_out, CEL, NotOutputEnableL);
  assign DataOutR = not_1_out ? ram_4_1_dataoutr : 8'bz;  // Controlled_Buffer controlled_buffer_2
  not not_1 (not_1_out, NotOutputEnableR);
endmodule

module fixed74181 (
  input  S1,
  input  S2,
  input  S3,
  input  S4,
  input  B4,
  input  A4,
  input  B3,
  input  A3,
  input  B2,
  input  A2,
  input  B1,
  input  A1,
  input  M,
  input  CIN,
  output G,
  output COUT,
  output P,
  output Y4,
  output Y3,
  output EQ,
  output Y2,
  output Y1
);

  wire and_1_out, and_2_out, and_3_out, and_4_out, and_5_out, and_6_out, and_7_out, and_8_out, and_9_out,
       and_10_out, and_11_out, and_12_out, and_13_out, and_14_out, and_15_out, and_16_out, and_17_out,
       and_18_out, and_19_out, and_20_out, and_21_out, and_22_out, and_23_out, and_24_out, and_25_out,
       and_26_out, and_27_out, and_28_out, buffer_1_out, buffer_2_out, buffer_3_out, buffer_4_out,
       buffer_5_out, nand_1_out, nand_3_out, nor_1_out, nor_2_out, nor_3_out, nor_4_out, nor_5_out,
       nor_6_out, nor_7_out, nor_8_out, nor_10_out, nor_11_out, nor_12_out, not_1_out, not_2_out, not_3_out,
       not_4_out, not_5_out, not_6_out, not_7_out, xor_1_out, xor_2_out, xor_3_out, xor_4_out;

  not not_1 (not_1_out, B4);
  not not_2 (not_2_out, B3);
  not not_3 (not_3_out, B2);
  not not_4 (not_4_out, B1);
  not not_5 (not_5_out, M);
  and and_1 (and_1_out, B4, S1, A4);
  and and_2 (and_2_out, A4, S2, not_1_out);
  and and_3 (and_3_out, not_1_out, S3);
  and and_4 (and_4_out, S4, B4);
  buf buffer_1 (buffer_1_out, A4);
  and and_5 (and_5_out, B3, S1, A3);
  and and_6 (and_6_out, A3, S2, not_2_out);
  and and_7 (and_7_out, not_2_out, S3);
  and and_8 (and_8_out, S4, B3);
  buf buffer_2 (buffer_2_out, A3);
  and and_9 (and_9_out, B2, S1, A2);
  and and_10 (and_10_out, A2, S2, not_3_out);
  and and_11 (and_11_out, not_3_out, S3);
  and and_12 (and_12_out, S4, B2);
  buf buffer_3 (buffer_3_out, A2);
  and and_13 (and_13_out, B1, S1, A1);
  and and_14 (and_14_out, A1, S2, not_4_out);
  and and_15 (and_15_out, not_4_out, S3);
  and and_16 (and_16_out, S4, B1);
  buf buffer_4 (buffer_4_out, A1);
  nor nor_1 (nor_1_out, and_1_out, and_2_out);
  nor nor_2 (nor_2_out, and_3_out, and_4_out, buffer_1_out);
  nor nor_3 (nor_3_out, and_5_out, and_6_out);
  nor nor_4 (nor_4_out, and_7_out, and_8_out, buffer_2_out);
  nor nor_5 (nor_5_out, and_9_out, and_10_out);
  nor nor_6 (nor_6_out, and_11_out, and_12_out, buffer_3_out);
  nor nor_7 (nor_7_out, and_13_out, and_14_out);
  nor nor_8 (nor_8_out, and_15_out, and_16_out, buffer_4_out);
  xor xor_1 (xor_1_out, nor_1_out, nor_2_out);
  xor xor_2 (xor_2_out, nor_3_out, nor_4_out);
  xor xor_3 (xor_3_out, nor_5_out, nor_6_out);
  xor xor_4 (xor_4_out, nor_7_out, nor_8_out);
  buf buffer_5 (buffer_5_out, nor_2_out);
  and and_17 (and_17_out, nor_1_out, nor_4_out);
  and and_18 (and_18_out, nor_1_out, nor_3_out, nor_6_out);
  and and_19 (and_19_out, nor_1_out, nor_3_out, nor_5_out, nor_8_out);
  nand nand_1 (nand_1_out, nor_1_out, nor_3_out, nor_5_out, nor_7_out, CIN);
  nand nand_2 (P, nor_1_out, nor_3_out, nor_5_out, nor_7_out);
  and and_20 (and_20_out, CIN, nor_7_out, nor_5_out, nor_3_out, not_5_out);
  and and_21 (and_21_out, nor_5_out, nor_3_out, nor_8_out, not_5_out);
  and and_22 (and_22_out, nor_3_out, nor_6_out, not_5_out);
  and and_23 (and_23_out, nor_4_out, not_5_out);
  and and_24 (and_24_out, CIN, nor_7_out, nor_5_out, not_5_out);
  and and_25 (and_25_out, nor_5_out, nor_8_out, not_5_out);
  and and_26 (and_26_out, nor_6_out, not_5_out);
  and and_27 (and_27_out, CIN, nor_7_out, not_5_out);
  and and_28 (and_28_out, nor_8_out, not_5_out);
  nand nand_3 (nand_3_out, CIN, not_5_out);
  nor nor_9 (G, buffer_5_out, and_17_out, and_18_out, and_19_out);
  nor nor_10 (nor_10_out, and_20_out, and_21_out, and_22_out, and_23_out);
  nor nor_11 (nor_11_out, and_24_out, and_25_out, and_26_out);
  nor nor_12 (nor_12_out, and_27_out, and_28_out);
  not not_6 (not_6_out, G);
  or or_1 (COUT, not_6_out, not_7_out);
  not not_7 (not_7_out, nand_1_out);
  xor xor_5 (Y4, xor_1_out, nor_10_out);
  xor xor_6 (Y3, xor_2_out, nor_11_out);
  xor xor_7 (Y2, xor_3_out, nor_12_out);
  xor xor_8 (Y1, xor_4_out, nand_3_out);
  and and_29 (EQ, Y3, Y4, Y1, Y2);
endmodule

module Memory (
  input  [15:0] AddressL,
  input  NotLoad,
  input  NotEnable,
  input  Clock,
  input  [7:0] DataIn,
  output [7:0] DataOut
);

  wire NotChipEnableRAM, NotChipEnableROM, NotChipEnableVRAM;
  wire [4:3] rom_1_data;

  // Probe on AddressL[14:0]
  RAM_62256 ram_62256_1 (
    .Address(AddressL[14:0]), .NotEnable(NotEnable), .NotLoad(NotLoad), .Clock(Clock), .DataIn(DataIn),
    .NotChipEnable(NotChipEnableRAM), .DataOut(DataOut));
  // Probe on {AddressL[15], AddressL[13:0]}
  ROM #(.addrWidth(15), .dataWidth(5)) rom_1 (
    .addr({AddressL[15], AddressL[13:0]}),
    .data({rom_1_data, NotChipEnableRAM, NotChipEnableROM, NotChipEnableVRAM}));
  EEPROM_ROM eeprom_rom_1 (
    .Address(AddressL[14:0]), .ChipEnable(NotChipEnableROM), .OutputEnable(NotEnable), .Data(DataOut));
  RAM_IDT7134 ram_idt7134_1 (
    .Clock(Clock), .DataInL(DataIn), .NotWriteRamL(NotLoad), .AddressL(AddressL), .CEL(NotChipEnableVRAM),
    .NotOutputEnableL(NotEnable), .NotOutputEnableR(1'b0), .DataOutL(DataOut));  // open: AddressR, DataOutR

  // Notes on the sheet:
  //   contents of rom_1 (hex, n*v repeats v):
  //   1024*1d 17 f 3070*1f 4096*1e 8192*1f 16384*1b
endmodule

module RAM_62256 (
  input  [14:0] Address,
  input  NotEnable,
  input  NotLoad,
  input  Clock,
  input  [7:0] DataIn,
  input  NotChipEnable,
  output [7:0] DataOut
);

  wire and_1_out, and_2_out, not_1_out, not_2_out, not_3_out;
  wire [7:0] ram_1_dout;

  not not_1 (not_1_out, NotLoad);
  and and_1 (and_1_out, not_1_out, not_2_out);
  not not_2 (not_2_out, NotChipEnable);
  not not_3 (not_3_out, NotEnable);
  and and_2 (and_2_out, not_2_out, not_3_out);
  POR por_1 ();  // open: out
  POR #(.PorHighDuration(1)) por_2 ();  // open: out
  RAM #(.addrWidth(15), .asyncread("true")) ram_1 (
    .addr(Address), .we(and_1_out), .oe(not_3_out), .clk(Clock), .din(DataIn), .dout(ram_1_dout));
  POR por_3 ();  // open: out
  assign DataOut = and_2_out ? ram_1_dout : 8'bz;  // Controlled_Buffer controlled_buffer_1
endmodule

module EEPROM_ROM (
  input  [14:0] Address,
  input  ChipEnable,
  input  OutputEnable,
  output [7:0] Data
);

  wire and_1_out, not_1_out, not_2_out;
  wire [7:0] rom_1_data;

  ROM #(.addrWidth(15)) rom_1 (.addr(Address), .data(rom_1_data));
  assign Data = and_1_out ? rom_1_data : 8'bz;  // Controlled_Buffer controlled_buffer_1
  and and_1 (and_1_out, not_1_out, not_2_out);
  not not_1 (not_1_out, ChipEnable);
  not not_2 (not_2_out, OutputEnable);

  // Notes on the sheet:
  //   contents of rom_1 (hex, n*v repeats v):
  //   1c 80 2c 0 5c 9 1c 80 2c 0 1c 80 2a 0 5c 60 1c 80 2c 0 3a 0 d0 0 2a 0 5c 0 2c 0 3a 0 d0 0 1c 80 2c 1
  //   3a 0 2c 0 2a 0 56 0 2c 0 3a 0 d0 0 1c 80 2c 2 3a 0 2c 0 2a 0 56 0 2c 0 3a 0 d0 0 2c 0 3a 0 4c 4 b0
  //   60 2c 2 56 0 2c 0 3a 0 2c 1 56 0 1c 0 2c 60 88 0 1c 80 2c 0 1c 80 2a 0 5c 6 1c 80 2c 0 3a 0 d0 0 1c
  //   80 2c 0 1c 80 2a 0 5c 5 1c 80 2c 0 3a 0 d0 0 1c 80 2c 0 3a 0 d0 f8 2a 0 4a 0 1c 80 2c 0 3a 0 a0 f8
  //   1c 80 3a 0 1c 0 2c b2 85 60 1c 80 2c 0 3a 0 a0 f8 5c 0 1c 0 2c bc 88 0 1c 80 2c 0 3a 0 a0 f8 5c 1 1c
  //   80 2c 0 1c 80 2a 0 5c 5 1c 80 2c 0 3a 0 d0 0 1c 80 2c 0 1c 80 2a 0 5c 5 1c 80 2c 0 3a 0 d0 0 1c 80
  //   2c 0 3a 0 d0 f8 2a 0 4a 0 1c 80 2c 0 3a 0 a0 f8 1c 80 3a 0 1c 1 2c e 85 60 1c 80 2c 0 3a 0 a0 f8 5c
  //   0 1c 1 2c 18 88 0 1c 80 2c 0 3a 0 a0 f8 5c 1 1c 80 2c 0 1c 80 2a 0 5c 4 1c 80 2c 0 3a 0 d0 0 1c 80
  //   2c 0 1c 80 2a 0 5c 5 1c 80 2c 0 3a 0 d0 0 1c 80 2c 0 3a 0 d0 f8 2a 0 4a 0 1c 80 2c 0 3a 0 a0 f8 1c
  //   80 3a 0 1c 1 2c 6a 85 60 1c 80 2c 0 3a 0 a0 f8 5c 0 1c 1 2c 74 88 0 1c 80 2c 0 3a 0 a0 f8 5c 1 1c 80
  //   2c 0 1c 80 2a 0 5c 6 1c 80 2c 0 3a 0 d0 0 1c 80 2c 0 1c 80 2a 0 5c 5 1c 80 2c 0 3a 0 d0 0 1c 80 2c 0
  //   3a 0 d0 f8 2a 0 4a 0 1c 80 2c 0 3a 0 a0 f8 1c 80 3a 0 1c 1 2c c6 81 60 1c 80 2c 0 3a 0 a0 f8 5c 0 1c
  //   1 2c d0 88 0 1c 80 2c 0 3a 0 a0 f8 5c 1 1c 80 2c 0 1c 80 2a 0 5c 5 1c 80 2c 0 3a 0 d0 0 1c 80 2c 0
  //   1c 80 2a 0 5c 5 1c 80 2c 0 3a 0 d0 0 1c 80 2c 0 3a 0 d0 f8 2a 0 4a 0 1c 80 2c 0 3a 0 a0 f8 1c 80 3a
  //   0 1c 2 2c 22 81 60 1c 80 2c 0 3a 0 a0 f8 5c 0 1c 2 2c 2c 88 0 1c 80 2c 0 3a 0 a0 f8 5c 1 1c 80 2c 0
  //   1c 80 2a 0 5c 4 1c 80 2c 0 3a 0 d0 0 1c 80 2c 0 1c 80 2a 0 5c 5 1c 80 2c 0 3a 0 d0 0 1c 80 2c 0 3a 0
  //   d0 f8 2a 0 4a 0 1c 80 2c 0 3a 0 a0 f8 1c 80 3a 0 1c 2 2c 7e 81 60 1c 80 2c 0 3a 0 a0 f8 5c 0 1c 2 2c
  //   88 88 0 1c 80 2c 0 3a 0 a0 f8 5c 1 1c 2 2c 88 88
endmodule

module ALU (
  input  NotEnable,
  input  [7:0] A,
  input  [7:0] B,
  input  [5:0] Operation,
  output NotCout,
  output Negative,
  output NotZero,
  output [7:0] DataOut
);

  wire fixed74181_1_cout, fixed74181_1_eq, fixed74181_1_g, fixed74181_1_p, fixed74181_2_eq, fixed74181_2_g,
       fixed74181_2_p;
  wire [2:0] fixed74181_2_y1;
  wire [3:0] fixed74181_1_y1;

  // Probe on A
  // Probe on B
  // NoConnect on fixed74181_1_g
  fixed74181 fixed74181_1 (
    .COUT(fixed74181_1_cout), .P(fixed74181_1_p), .Y4(fixed74181_1_y1[3]), .Y3(fixed74181_1_y1[2]),
    .G(fixed74181_1_g), .EQ(fixed74181_1_eq), .Y2(fixed74181_1_y1[1]), .Y1(fixed74181_1_y1[0]),
    .S4(Operation[2]), .S1(Operation[5]), .B4(B[3]), .A4(A[3]), .B3(B[2]), .S2(Operation[4]), .A3(A[2]),
    .B2(B[1]), .A2(A[1]), .B1(B[0]), .S3(Operation[3]), .A1(A[0]), .M(Operation[0]), .CIN(Operation[1]));
  // NoConnect on fixed74181_1_p
  // NoConnect on fixed74181_1_eq
  // NoConnect on fixed74181_2_g
  fixed74181 fixed74181_2 (
    .COUT(NotCout), .P(fixed74181_2_p), .Y4(Negative), .Y3(fixed74181_2_y1[2]), .G(fixed74181_2_g),
    .EQ(fixed74181_2_eq), .Y2(fixed74181_2_y1[1]), .Y1(fixed74181_2_y1[0]), .S4(Operation[2]),
    .S1(Operation[5]), .B4(B[7]), .A4(A[7]), .B3(B[6]), .S2(Operation[4]), .A3(A[6]), .B2(B[5]), .A2(A[5]),
    .B1(B[4]), .S3(Operation[3]), .A1(A[4]), .M(Operation[0]), .CIN(fixed74181_1_cout));
  // NoConnect on fixed74181_2_p
  // NoConnect on fixed74181_2_eq
  // Probe on {Negative, fixed74181_2_y1, fixed74181_1_y1}
  OctalTransceiver74245 octaltransceiver74245_1 (
    .B_Out({Negative, fixed74181_2_y1, fixed74181_1_y1}), .A_out(DataOut), .Dir(1'b0), .NotEnable(NotEnable),
    .B_in({Negative, fixed74181_2_y1, fixed74181_1_y1}), .A_in(DataOut));
  Comparator74682 comparator74682_1 (
    .B({8{1'b0}}), .A({Negative, fixed74181_2_y1, fixed74181_1_y1}), .NotAEqualsB(NotZero));

  // Other names for the same wires on the sheet: A1 = A[0]; A2 = A[1]; A3 = A[2]; A4 = A[3]; A5 = A[4]; A6 = A[5];
  //   A7 = A[6]; A8 = A[7]; B1 = B[0]; B2 = B[1]; B3 = B[2]; B4 = B[3]; B5 = B[4]; B6 = B[5]; B7 = B[6]; B8 = B[7];
  //   NotM = Operation[0]; NotCIN = Operation[1]; Sel[3:0] = Operation[5:2]
endmodule

module Comparator74682 (
  input  [7:0] B,
  input  [7:0] A,
  output NotAEqualsB
);

  wire n7485_1_pin2, n7485_1_pin6, n7485_2_pin6;

  _7485 #(.ShowInternalStructure("true")) u_7485_1 (
    .pin1(B[7]), .pin2(n7485_1_pin2), .pin3(n7485_1_pin2), .pin4(n7485_1_pin2), .pin6(n7485_1_pin6),
    .pin15(A[7]), .pin14(B[6]), .pin13(A[6]), .pin12(A[5]), .pin11(B[5]), .pin10(A[4]), .pin9(B[4]));  // open: pin5, pin7
  nand nand_1 (NotAEqualsB, n7485_1_pin6, n7485_2_pin6);
  _7485 #(.ShowInternalStructure("true")) u_7485_2 (
    .pin1(B[3]), .pin2(n7485_1_pin2), .pin3(n7485_1_pin2), .pin4(n7485_1_pin2), .pin6(n7485_2_pin6),
    .pin15(A[3]), .pin14(B[2]), .pin13(A[2]), .pin12(A[1]), .pin11(A[2]), .pin10(A[0]), .pin9(B[0]));  // open: pin5, pin7

  assign B[1] = A[2];
  // also tied to VCC on the sheet: n7485_1_pin2
endmodule
